// Digital circuit BR 16x32.dig as structural Verilog
module BR_16x32 (
  input  [3:0] c,
  input  En,
  input  Clk,
  input  [31:0] C_2,
  input  [3:0] a,
  input  [3:0] b,
  output [31:0] A_2,
  output [31:0] B_2
);

  wire demultiplexer_1_out_0, demultiplexer_1_out_1, demultiplexer_1_out_2, demultiplexer_1_out_3,
       demultiplexer_1_out_4, demultiplexer_1_out_5, demultiplexer_1_out_6, demultiplexer_1_out_7,
       demultiplexer_1_out_8, demultiplexer_1_out_9, demultiplexer_1_out_10, demultiplexer_1_out_11,
       demultiplexer_1_out_12, demultiplexer_1_out_13, demultiplexer_1_out_14, demultiplexer_1_out_15;
  wire [31:0] s0, s1, s2, s3, s4, s5, s6, s7, s8, s9, s10, s11, s12, s13, s14, s15;

  Demultiplexer #(.Selector_Bits(4)) demultiplexer_1 (
    .sel(c), .in(En), .out_0(demultiplexer_1_out_0), .out_1(demultiplexer_1_out_1),
    .out_2(demultiplexer_1_out_2), .out_3(demultiplexer_1_out_3), .out_4(demultiplexer_1_out_4),
    .out_5(demultiplexer_1_out_5), .out_6(demultiplexer_1_out_6), .out_7(demultiplexer_1_out_7),
    .out_8(demultiplexer_1_out_8), .out_9(demultiplexer_1_out_9), .out_10(demultiplexer_1_out_10),
    .out_11(demultiplexer_1_out_11), .out_12(demultiplexer_1_out_12), .out_13(demultiplexer_1_out_13),
    .out_14(demultiplexer_1_out_14), .out_15(demultiplexer_1_out_15));
  Registrador_32bits registrador_32bits_1 (.En(demultiplexer_1_out_0), .Clk(Clk), .E({32{1'b0}}), .S(s0));
  Registrador_32bits registrador_32bits_2 (.En(demultiplexer_1_out_1), .Clk(Clk), .E(C_2), .S(s1));
  Registrador_32bits registrador_32bits_3 (.En(demultiplexer_1_out_2), .Clk(Clk), .E(C_2), .S(s2));
  Registrador_32bits registrador_32bits_4 (.En(demultiplexer_1_out_3), .Clk(Clk), .E(C_2), .S(s3));
  Registrador_32bits registrador_32bits_5 (.En(demultiplexer_1_out_4), .Clk(Clk), .E(C_2), .S(s4));
  Registrador_32bits registrador_32bits_6 (.En(demultiplexer_1_out_5), .Clk(Clk), .E(C_2), .S(s5));
  Registrador_32bits registrador_32bits_7 (.En(demultiplexer_1_out_6), .Clk(Clk), .E(C_2), .S(s6));
  Registrador_32bits registrador_32bits_8 (.En(demultiplexer_1_out_7), .Clk(Clk), .E(C_2), .S(s7));
  Registrador_32bits registrador_32bits_9 (.En(demultiplexer_1_out_8), .Clk(Clk), .E(C_2), .S(s8));
  Registrador_32bits registrador_32bits_10 (.En(demultiplexer_1_out_9), .Clk(Clk), .E(C_2), .S(s9));
  Registrador_32bits registrador_32bits_11 (.En(demultiplexer_1_out_10), .Clk(Clk), .E(C_2), .S(s10));
  Registrador_32bits registrador_32bits_12 (.En(demultiplexer_1_out_11), .Clk(Clk), .E(C_2), .S(s11));
  Registrador_32bits registrador_32bits_13 (.En(demultiplexer_1_out_12), .Clk(Clk), .E(C_2), .S(s12));
  Registrador_32bits registrador_32bits_14 (.En(demultiplexer_1_out_13), .Clk(Clk), .E(C_2), .S(s13));
  Registrador_32bits registrador_32bits_15 (.En(demultiplexer_1_out_14), .Clk(Clk), .E(C_2), .S(s14));
  Registrador_32bits registrador_32bits_16 (.En(demultiplexer_1_out_15), .Clk(Clk), .E(C_2), .S(s15));
  Multiplexer #(.Selector_Bits(4), .Bits(32)) multiplexer_1 (
    .sel(a), .in_0(s0), .in_1(s1), .in_2(s2), .in_3(s3), .in_4(s4), .in_5(s5), .in_6(s6), .in_7(s7),
    .in_8(s8), .in_9(s9), .in_10(s10), .in_11(s11), .in_12(s12), .in_13(s13), .in_14(s14), .in_15(s15),
    .out(A_2));
  Multiplexer #(.Selector_Bits(4), .Bits(32)) multiplexer_2 (
    .sel(b), .in_0(s0), .in_1(s1), .in_2(s2), .in_3(s3), .in_4(s4), .in_5(s5), .in_6(s6), .in_7(s7),
    .in_8(s8), .in_9(s9), .in_10(s10), .in_11(s11), .in_12(s12), .in_13(s13), .in_14(s14), .in_15(s15),
    .out(B_2));

  // Notes on the sheet:
  //   Registrador zero contém valor lógico 0
endmodule
