// Digital circuit Display 11 Saídas.dig as structural Verilog
module \Display_11_Saídas  (
  input  [31:0] D,
  input  Dis,
  output [31:0] s0,
  output [31:0] s1,
  output [31:0] s2,
  output [31:0] s3,
  output [31:0] s4,
  output [31:0] s5,
  output [31:0] s6,
  output [31:0] s7,
  output [31:0] s8,
  output [31:0] s9,
  output [31:0] s10
);

  D_FF #(.Bits(32)) d_ff_1 (.D(D), .C(Dis), .Q(s0));  // open: nQ
  D_FF #(.Bits(32)) d_ff_2 (.D(s0), .C(Dis), .Q(s1));  // open: nQ
  D_FF #(.Bits(32)) d_ff_3 (.D(s1), .C(Dis), .Q(s2));  // open: nQ
  D_FF #(.Bits(32)) d_ff_4 (.D(s2), .C(Dis), .Q(s3));  // open: nQ
  D_FF #(.Bits(32)) d_ff_5 (.D(s3), .C(Dis), .Q(s4));  // open: nQ
  D_FF #(.Bits(32)) d_ff_6 (.D(s4), .C(Dis), .Q(s5));  // open: nQ
  D_FF #(.Bits(32)) d_ff_7 (.D(s5), .C(Dis), .Q(s6));  // open: nQ
  D_FF #(.Bits(32)) d_ff_8 (.D(s6), .C(Dis), .Q(s7));  // open: nQ
  D_FF #(.Bits(32)) d_ff_9 (.D(s7), .C(Dis), .Q(s8));  // open: nQ
  D_FF #(.Bits(32)) d_ff_10 (.D(s8), .C(Dis), .Q(s9));  // open: nQ
  D_FF #(.Bits(32)) d_ff_11 (.D(s9), .C(Dis), .Q(s10));  // open: nQ

  // Other names for the same wires on the sheet: Display = Dis
endmodule
