// Digital circuit Eq.dig as structural Verilog
module Eq (
  input  [31:0] A,
  input  [31:0] B,
  output S
);

  wire e16;
  wire [31:0] xnor_1_out;

  assign {xnor_1_out[31:17], e16, xnor_1_out[15:0]} = ~(A ^ B);  // XNOr xnor_1, 32 bits wide
  and and_1 (S, xnor_1_out[0], xnor_1_out[1], xnor_1_out[2], xnor_1_out[3], xnor_1_out[4], xnor_1_out[5], xnor_1_out[6], xnor_1_out[7], xnor_1_out[8], xnor_1_out[9], xnor_1_out[10], xnor_1_out[11], xnor_1_out[12], xnor_1_out[13], xnor_1_out[14], xnor_1_out[15], xnor_1_out[17], xnor_1_out[18], xnor_1_out[19], xnor_1_out[20], xnor_1_out[21], xnor_1_out[22], xnor_1_out[23], xnor_1_out[24], xnor_1_out[25], xnor_1_out[26], xnor_1_out[27], xnor_1_out[28], xnor_1_out[29], xnor_1_out[30], xnor_1_out[31], e16);
endmodule
