// Digital circuit Full-Adder 1bit.dig as structural Verilog
module Full_Adder_1bit (
  input  [31:0] A,
  input  [31:0] B,
  input  cin,
  output cout,
  output S
);

  wire and_1_out, and_2_out, or_1_out;

  xor xor_1 (S, B[0], A[0], cin);
  and and_1 (and_1_out, A[0], B[0]);
  or or_1 (or_1_out, A[0], B[0]);
  and and_2 (and_2_out, or_1_out, cin);
  or or_2 (cout, and_1_out, and_2_out);
  // Pins of 1 and 32 bits meet at A
  // Pins of 1 and 32 bits meet at B
endmodule
