// Digital circuit Full-Adder 32bits.dig as structural Verilog
module Full_Adder_32bits (
  input  [31:0] A,
  input  [31:0] B,
  output [31:0] S,
  output cout
);

  wire full_adder_1bit_1_p4, full_adder_1bit_2_p4, full_adder_1bit_3_p4, full_adder_1bit_4_p4,
       full_adder_1bit_5_p4, full_adder_1bit_6_p4, full_adder_1bit_7_p4, full_adder_1bit_8_p4,
       full_adder_1bit_9_p4, full_adder_1bit_10_p4, full_adder_1bit_11_p4, full_adder_1bit_12_p4,
       full_adder_1bit_13_p4, full_adder_1bit_14_p4, full_adder_1bit_15_p4, full_adder_1bit_16_p4,
       full_adder_1bit_17_p4, full_adder_1bit_18_p4, full_adder_1bit_19_p4, full_adder_1bit_20_p4,
       full_adder_1bit_21_p4, full_adder_1bit_22_p4, full_adder_1bit_23_p4, full_adder_1bit_24_p4,
       full_adder_1bit_25_p4, full_adder_1bit_26_p4, full_adder_1bit_27_p4, full_adder_1bit_28_p4,
       full_adder_1bit_29_p4, full_adder_1bit_30_p4, full_adder_1bit_31_p4;

  // Full_Adder_1bit full_adder_1bit_1: pin names not known; wires that end beside it: A[0], B[0], 1'b0, full_adder_1bit_1_p4, S[0]
  // Full_Adder_1bit full_adder_1bit_2: pin names not known; wires that end beside it: A[1], B[1], full_adder_1bit_1_p4, full_adder_1bit_2_p4, S[1]
  // Full_Adder_1bit full_adder_1bit_3: pin names not known; wires that end beside it: A[2], B[2], full_adder_1bit_2_p4, full_adder_1bit_3_p4, S[2]
  // Full_Adder_1bit full_adder_1bit_4: pin names not known; wires that end beside it: A[3], B[3], full_adder_1bit_3_p4, full_adder_1bit_4_p4, S[3]
  // Full_Adder_1bit full_adder_1bit_5: pin names not known; wires that end beside it: A[4], B[4], full_adder_1bit_4_p4, full_adder_1bit_5_p4, S[4]
  // Full_Adder_1bit full_adder_1bit_6: pin names not known; wires that end beside it: A[5], B[5], full_adder_1bit_5_p4, full_adder_1bit_6_p4, S[5]
  // Full_Adder_1bit full_adder_1bit_7: pin names not known; wires that end beside it: A[6], B[6], full_adder_1bit_6_p4, full_adder_1bit_7_p4, S[6]
  // Full_Adder_1bit full_adder_1bit_8: pin names not known; wires that end beside it: A[7], B[7], full_adder_1bit_7_p4, full_adder_1bit_8_p4, S[7]
  // Full_Adder_1bit full_adder_1bit_9: pin names not known; wires that end beside it: A[8], B[8], full_adder_1bit_8_p4, full_adder_1bit_9_p4, S[8]
  // Full_Adder_1bit full_adder_1bit_10: pin names not known; wires that end beside it: A[9], B[9], full_adder_1bit_9_p4, full_adder_1bit_10_p4, S[9]
  // Full_Adder_1bit full_adder_1bit_11: pin names not known; wires that end beside it: A[10], B[10], full_adder_1bit_10_p4, full_adder_1bit_11_p4, S[10]
  // Full_Adder_1bit full_adder_1bit_12: pin names not known; wires that end beside it: A[11], B[11], full_adder_1bit_11_p4, full_adder_1bit_12_p4, S[11]
  // Full_Adder_1bit full_adder_1bit_13: pin names not known; wires that end beside it: A[12], B[12], full_adder_1bit_12_p4, full_adder_1bit_13_p4, S[12]
  // Full_Adder_1bit full_adder_1bit_14: pin names not known; wires that end beside it: A[13], B[13], full_adder_1bit_13_p4, full_adder_1bit_14_p4, S[13]
  // Full_Adder_1bit full_adder_1bit_15: pin names not known; wires that end beside it: A[14], B[14], full_adder_1bit_14_p4, full_adder_1bit_15_p4, S[14]
  // Full_Adder_1bit full_adder_1bit_16: pin names not known; wires that end beside it: A[15], B[15], full_adder_1bit_15_p4, full_adder_1bit_16_p4, S[15]
  // Full_Adder_1bit full_adder_1bit_17: pin names not known; wires that end beside it: A[16], B[16], full_adder_1bit_16_p4, full_adder_1bit_17_p4, S[16]
  // Full_Adder_1bit full_adder_1bit_18: pin names not known; wires that end beside it: A[17], B[17], full_adder_1bit_17_p4, full_adder_1bit_18_p4, S[17]
  // Full_Adder_1bit full_adder_1bit_19: pin names not known; wires that end beside it: A[18], B[18], full_adder_1bit_18_p4, full_adder_1bit_19_p4, S[18]
  // Full_Adder_1bit full_adder_1bit_20: pin names not known; wires that end beside it: A[19], B[19], full_adder_1bit_19_p4, full_adder_1bit_20_p4, S[19]
  // Full_Adder_1bit full_adder_1bit_21: pin names not known; wires that end beside it: A[20], B[20], full_adder_1bit_20_p4, full_adder_1bit_21_p4, S[20]
  // Full_Adder_1bit full_adder_1bit_22: pin names not known; wires that end beside it: A[21], B[21], full_adder_1bit_21_p4, full_adder_1bit_22_p4, S[21]
  // Full_Adder_1bit full_adder_1bit_23: pin names not known; wires that end beside it: A[22], B[22], full_adder_1bit_22_p4, full_adder_1bit_23_p4, S[22]
  // Full_Adder_1bit full_adder_1bit_24: pin names not known; wires that end beside it: A[23], B[23], full_adder_1bit_23_p4, full_adder_1bit_24_p4, S[23]
  // Full_Adder_1bit full_adder_1bit_25: pin names not known; wires that end beside it: A[24], B[24], full_adder_1bit_24_p4, full_adder_1bit_25_p4, S[24]
  // Full_Adder_1bit full_adder_1bit_26: pin names not known; wires that end beside it: A[25], B[25], full_adder_1bit_25_p4, full_adder_1bit_26_p4, S[25]
  // Full_Adder_1bit full_adder_1bit_27: pin names not known; wires that end beside it: A[26], B[26], full_adder_1bit_26_p4, full_adder_1bit_27_p4, S[26]
  // Full_Adder_1bit full_adder_1bit_28: pin names not known; wires that end beside it: A[27], B[27], full_adder_1bit_27_p4, full_adder_1bit_28_p4, S[27]
  // Full_Adder_1bit full_adder_1bit_29: pin names not known; wires that end beside it: A[28], B[28], full_adder_1bit_28_p4, full_adder_1bit_29_p4, S[28]
  // Full_Adder_1bit full_adder_1bit_30: pin names not known; wires that end beside it: A[29], B[29], full_adder_1bit_29_p4, full_adder_1bit_30_p4, S[29]
  // Full_Adder_1bit full_adder_1bit_31: pin names not known; wires that end beside it: A[30], B[30], full_adder_1bit_30_p4, full_adder_1bit_31_p4, S[30]
  // Full_Adder_1bit full_adder_1bit_32: pin names not known; wires that end beside it: A[31], B[31], full_adder_1bit_31_p4, cout, S[31]
endmodule
