// Digital circuit Full-Subtractor 1bit.dig as structural Verilog
module Full_Subtractor_1bit (
  input  A,
  input  B,
  input  bin,
  output S,
  output bout
);

  wire and_1_out, and_2_out, and_3_out, not_1_out, xor_1_out;

  xor xor_1 (xor_1_out, B, A);
  xor xor_2 (S, xor_1_out, bin);
  not not_1 (not_1_out, A);
  and and_1 (and_1_out, not_1_out, B);
  and and_2 (and_2_out, bin, not_1_out);
  and and_3 (and_3_out, B, bin);
  or or_1 (bout, and_1_out, and_2_out, and_3_out);
endmodule
