// Digital circuit Full-Subtractor 32bits.dig as structural Verilog
module Full_Subtractor_32bits (
  input  [31:0] A,
  input  [31:0] B,
  output [31:0] S,
  output bout
);

  wire full_subtractor_1bit_2_bout, full_subtractor_1bit_3_bout, full_subtractor_1bit_4_bout,
       full_subtractor_1bit_5_bout, full_subtractor_1bit_6_bout, full_subtractor_1bit_7_bout,
       full_subtractor_1bit_8_bout, full_subtractor_1bit_9_bout, full_subtractor_1bit_10_bout,
       full_subtractor_1bit_11_bout, full_subtractor_1bit_12_bout, full_subtractor_1bit_13_bout,
       full_subtractor_1bit_14_bout, full_subtractor_1bit_15_bout, full_subtractor_1bit_16_bout,
       full_subtractor_1bit_17_bout, full_subtractor_1bit_18_bout, full_subtractor_1bit_19_bout,
       full_subtractor_1bit_20_bout, full_subtractor_1bit_21_bout, full_subtractor_1bit_22_bout,
       full_subtractor_1bit_23_bout, full_subtractor_1bit_24_bout, full_subtractor_1bit_25_bout,
       full_subtractor_1bit_26_bout, full_subtractor_1bit_27_bout, full_subtractor_1bit_28_bout,
       full_subtractor_1bit_29_bout, full_subtractor_1bit_30_bout, full_subtractor_1bit_31_bout,
       full_subtractor_1bit_32_bout;

  Full_Subtractor_1bit full_subtractor_1bit_1 (
    .A(A[31]), .B(B[31]), .bin(full_subtractor_1bit_2_bout), .S(S[0]), .bout(bout));
  Full_Subtractor_1bit full_subtractor_1bit_2 (
    .A(A[30]), .B(B[30]), .bin(full_subtractor_1bit_3_bout), .S(S[1]), .bout(full_subtractor_1bit_2_bout));
  Full_Subtractor_1bit full_subtractor_1bit_3 (
    .A(A[29]), .B(B[29]), .bin(full_subtractor_1bit_4_bout), .S(S[2]), .bout(full_subtractor_1bit_3_bout));
  Full_Subtractor_1bit full_subtractor_1bit_4 (
    .A(A[28]), .B(B[28]), .bin(full_subtractor_1bit_5_bout), .S(S[3]), .bout(full_subtractor_1bit_4_bout));
  Full_Subtractor_1bit full_subtractor_1bit_5 (
    .A(A[27]), .B(B[27]), .bin(full_subtractor_1bit_6_bout), .S(S[4]), .bout(full_subtractor_1bit_5_bout));
  Full_Subtractor_1bit full_subtractor_1bit_6 (
    .A(A[26]), .B(B[26]), .bin(full_subtractor_1bit_7_bout), .S(S[5]), .bout(full_subtractor_1bit_6_bout));
  Full_Subtractor_1bit full_subtractor_1bit_7 (
    .A(A[25]), .B(B[25]), .bin(full_subtractor_1bit_8_bout), .S(S[6]), .bout(full_subtractor_1bit_7_bout));
  Full_Subtractor_1bit full_subtractor_1bit_8 (
    .A(A[24]), .B(B[24]), .bin(full_subtractor_1bit_9_bout), .S(S[7]), .bout(full_subtractor_1bit_8_bout));
  Full_Subtractor_1bit full_subtractor_1bit_9 (
    .A(A[23]), .B(B[23]), .bin(full_subtractor_1bit_10_bout), .S(S[8]), .bout(full_subtractor_1bit_9_bout));
  Full_Subtractor_1bit full_subtractor_1bit_10 (
    .A(A[22]), .B(B[22]), .bin(full_subtractor_1bit_11_bout), .S(S[9]), .bout(full_subtractor_1bit_10_bout));
  Full_Subtractor_1bit full_subtractor_1bit_11 (
    .A(A[21]), .B(B[21]), .bin(full_subtractor_1bit_12_bout), .S(S[10]), .bout(full_subtractor_1bit_11_bout));
  Full_Subtractor_1bit full_subtractor_1bit_12 (
    .A(A[20]), .B(B[20]), .bin(full_subtractor_1bit_13_bout), .S(S[11]), .bout(full_subtractor_1bit_12_bout));
  Full_Subtractor_1bit full_subtractor_1bit_13 (
    .A(A[19]), .B(B[19]), .bin(full_subtractor_1bit_14_bout), .S(S[12]), .bout(full_subtractor_1bit_13_bout));
  Full_Subtractor_1bit full_subtractor_1bit_14 (
    .A(A[18]), .B(B[18]), .bin(full_subtractor_1bit_15_bout), .S(S[13]), .bout(full_subtractor_1bit_14_bout));
  Full_Subtractor_1bit full_subtractor_1bit_15 (
    .A(A[17]), .B(B[17]), .bin(full_subtractor_1bit_16_bout), .S(S[14]), .bout(full_subtractor_1bit_15_bout));
  Full_Subtractor_1bit full_subtractor_1bit_16 (
    .A(A[16]), .B(B[16]), .bin(full_subtractor_1bit_17_bout), .S(S[15]), .bout(full_subtractor_1bit_16_bout));
  Full_Subtractor_1bit full_subtractor_1bit_17 (
    .A(A[15]), .B(B[15]), .bin(full_subtractor_1bit_18_bout), .S(S[16]), .bout(full_subtractor_1bit_17_bout));
  Full_Subtractor_1bit full_subtractor_1bit_18 (
    .A(A[14]), .B(B[14]), .bin(full_subtractor_1bit_19_bout), .S(S[17]), .bout(full_subtractor_1bit_18_bout));
  Full_Subtractor_1bit full_subtractor_1bit_19 (
    .A(A[13]), .B(B[13]), .bin(full_subtractor_1bit_20_bout), .S(S[18]), .bout(full_subtractor_1bit_19_bout));
  Full_Subtractor_1bit full_subtractor_1bit_20 (
    .A(A[12]), .B(B[12]), .bin(full_subtractor_1bit_21_bout), .S(S[19]), .bout(full_subtractor_1bit_20_bout));
  Full_Subtractor_1bit full_subtractor_1bit_21 (
    .A(A[11]), .B(B[11]), .bin(full_subtractor_1bit_22_bout), .S(S[20]), .bout(full_subtractor_1bit_21_bout));
  Full_Subtractor_1bit full_subtractor_1bit_22 (
    .A(A[10]), .B(B[10]), .bin(full_subtractor_1bit_23_bout), .S(S[21]), .bout(full_subtractor_1bit_22_bout));
  Full_Subtractor_1bit full_subtractor_1bit_23 (
    .A(A[9]), .B(B[9]), .bin(full_subtractor_1bit_24_bout), .S(S[22]), .bout(full_subtractor_1bit_23_bout));
  Full_Subtractor_1bit full_subtractor_1bit_24 (
    .A(A[8]), .B(B[8]), .bin(full_subtractor_1bit_25_bout), .S(S[23]), .bout(full_subtractor_1bit_24_bout));
  Full_Subtractor_1bit full_subtractor_1bit_25 (
    .A(A[7]), .B(B[7]), .bin(full_subtractor_1bit_26_bout), .S(S[24]), .bout(full_subtractor_1bit_25_bout));
  Full_Subtractor_1bit full_subtractor_1bit_26 (
    .A(A[6]), .B(B[6]), .bin(full_subtractor_1bit_27_bout), .S(S[25]), .bout(full_subtractor_1bit_26_bout));
  Full_Subtractor_1bit full_subtractor_1bit_27 (
    .A(A[5]), .B(B[5]), .bin(full_subtractor_1bit_28_bout), .S(S[26]), .bout(full_subtractor_1bit_27_bout));
  Full_Subtractor_1bit full_subtractor_1bit_28 (
    .A(A[4]), .B(B[4]), .bin(full_subtractor_1bit_29_bout), .S(S[27]), .bout(full_subtractor_1bit_28_bout));
  Full_Subtractor_1bit full_subtractor_1bit_29 (
    .A(A[3]), .B(B[3]), .bin(full_subtractor_1bit_30_bout), .S(S[28]), .bout(full_subtractor_1bit_29_bout));
  Full_Subtractor_1bit full_subtractor_1bit_30 (
    .A(A[2]), .B(B[2]), .bin(full_subtractor_1bit_31_bout), .S(S[29]), .bout(full_subtractor_1bit_30_bout));
  Full_Subtractor_1bit full_subtractor_1bit_31 (
    .A(A[1]), .B(B[1]), .bin(full_subtractor_1bit_32_bout), .S(S[30]), .bout(full_subtractor_1bit_31_bout));
  Full_Subtractor_1bit full_subtractor_1bit_32 (
    .A(A[0]), .B(B[0]), .bin(1'b0), .S(S[31]), .bout(full_subtractor_1bit_32_bout));
endmodule
