// Digital circuit Main.dig as structural Verilog
module Main (
  input  clk
);

  wire ALUSrc, and_1_out, Branch, Desvio, Display, Halt, Jump, not_1_out, RegWrite, ula_32bits_1_zero;
  wire [3:0] a, b, c, Funct;
  wire [15:0] Const;
  wire [31:0] br_16x32_1_a_2, br_16x32_1_b_2, d_ff_1_q, d_ff_2_q, d_ff_3_q, d_ff_4_q, d_ff_5_q, d_ff_6_q,
       d_ff_7_q, d_ff_8_q, d_ff_9_q, d_ff_10_q, d_ff_11_q, extsign_1_s, extzero_1_s, full_adder_32bits_1_s,
       full_adder_32bits_2_s, multiplexer_1_out, multiplexer_2_out, multiplexer_3_out, PC_s, ula_32bits_1_s;
  wire [31:28] rom_1_d;

  Multiplexer #(.Bits(32)) multiplexer_1 (.sel(Halt), .in_0(32'h1), .in_1({32{1'b0}}), .out(multiplexer_1_out));
  Full_Adder_32bits full_adder_32bits_1 (.A(multiplexer_1_out), .B(PC_s), .S(full_adder_32bits_1_s));  // open: cout
  Full_Adder_32bits full_adder_32bits_2 (.A(extsign_1_s), .B(PC_s), .S(full_adder_32bits_2_s));  // open: cout
  Multiplexer #(.Bits(32)) multiplexer_2 (
    .sel(Desvio), .in_0(full_adder_32bits_1_s), .in_1(full_adder_32bits_2_s), .out(multiplexer_2_out));
  Registrador_32bits PC (.En(1'b1), .Clk(clk), .E(multiplexer_2_out), .S(PC_s));
  ROM #(.AddrBits(24), .Bits(32)) rom_1 (.A(PC_s[23:0]), .sel(1'b1), .D({rom_1_d, c, b, a, Const}));
  ExtSign extsign_1 (.A(Const), .S(extsign_1_s));
  ROM #(.AddrBits(4), .Bits(10)) rom_2 (
    .A(rom_1_d), .sel(1'b1), .D({Funct, RegWrite, ALUSrc, Branch, Display, Halt, Jump}));
  BR_16x32 br_16x32_1 (
    .c(c), .En(RegWrite), .Clk(clk), .C_2(ula_32bits_1_s), .a(a), .b(b), .A_2(br_16x32_1_a_2),
    .B_2(br_16x32_1_b_2));
  ExtZero extzero_1 (.A(Const), .S(extzero_1_s));
  D_FF #(.Bits(32)) d_ff_1 (.D(br_16x32_1_a_2), .C(Display), .Q(d_ff_1_q));  // open: nQ
  Multiplexer #(.Bits(32)) multiplexer_3 (
    .sel(ALUSrc), .in_0(br_16x32_1_b_2), .in_1(extzero_1_s), .out(multiplexer_3_out));
  // Probe on d_ff_1_q
  D_FF #(.Bits(32)) d_ff_2 (.D(d_ff_1_q), .C(Display), .Q(d_ff_2_q));  // open: nQ
  // Probe on d_ff_2_q
  D_FF #(.Bits(32)) d_ff_3 (.D(d_ff_2_q), .C(Display), .Q(d_ff_3_q));  // open: nQ
  ULA_32bits ula_32bits_1 (
    .A(br_16x32_1_a_2), .B(multiplexer_3_out), .funct(Funct), .S(ula_32bits_1_s), .Zero(ula_32bits_1_zero));
  // Probe on d_ff_3_q
  D_FF #(.Bits(32)) d_ff_4 (.D(d_ff_3_q), .C(Display), .Q(d_ff_4_q));  // open: nQ
  not not_1 (not_1_out, ula_32bits_1_zero);
  // Probe on d_ff_4_q
  D_FF #(.Bits(32)) d_ff_5 (.D(d_ff_4_q), .C(Display), .Q(d_ff_5_q));  // open: nQ
  and and_1 (and_1_out, not_1_out, Branch);
  // Probe on d_ff_5_q
  D_FF #(.Bits(32)) d_ff_6 (.D(d_ff_5_q), .C(Display), .Q(d_ff_6_q));  // open: nQ
  or or_1 (Desvio, and_1_out, Jump);
  // Probe on d_ff_6_q
  D_FF #(.Bits(32)) d_ff_7 (.D(d_ff_6_q), .C(Display), .Q(d_ff_7_q));  // open: nQ
  // Probe on d_ff_7_q
  D_FF #(.Bits(32)) d_ff_8 (.D(d_ff_7_q), .C(Display), .Q(d_ff_8_q));  // open: nQ
  // Probe on d_ff_8_q
  D_FF #(.Bits(32)) d_ff_9 (.D(d_ff_8_q), .C(Display), .Q(d_ff_9_q));  // open: nQ
  // Probe on d_ff_9_q
  D_FF #(.Bits(32)) d_ff_10 (.D(d_ff_9_q), .C(Display), .Q(d_ff_10_q));  // open: nQ
  // Probe on d_ff_10_q
  D_FF #(.Bits(32)) d_ff_11 (.D(d_ff_10_q), .C(Display), .Q(d_ff_11_q));  // open: nQ
  // Probe on d_ff_11_q

  // Notes on the sheet:
  //   clk: Hz: 10
  //   contents of rom_1 (hex, n*v repeats v):
  //   0,1100000a,12000007,13000012,14000000,15000000,c0510007,46530000
  //   ,26620000,24460000,d0040000,95050001,b000fffa,d0040000,e0000000
  //   ,89*0,e0000
  //   contents of rom_2 (hex, n*v repeats v):
  //   0,1f0,20,60,a0,e0,120,160,1a0,30,70,11,48,254,252
endmodule
