// Digital circuit Mul 32bits.dig as structural Verilog
module Mul_32bits (
  input  [31:0] A,
  input  [31:0] B,
  output [31:0] S
);

  wire [63:32] mul_1_mul;

  Mul #(.Signed("true"), .Bits(32)) mul_1 (.a(A), .b(B), .mul({mul_1_mul, S}));
endmodule
