// Digital circuit Registrador 32bits.dig as structural Verilog
module Registrador_32bits (
  input  En,
  input  Clk,
  input  [31:0] E,
  output [31:0] S
);

  wire multiplexer_1_out, multiplexer_2_out, multiplexer_3_out, multiplexer_4_out, multiplexer_5_out,
       multiplexer_6_out, multiplexer_7_out, multiplexer_8_out, multiplexer_9_out, multiplexer_10_out,
       multiplexer_11_out, multiplexer_12_out, multiplexer_13_out, multiplexer_14_out, multiplexer_15_out,
       multiplexer_16_out, multiplexer_17_out, multiplexer_18_out, multiplexer_19_out, multiplexer_20_out,
       multiplexer_21_out, multiplexer_22_out, multiplexer_23_out, multiplexer_24_out, multiplexer_25_out,
       multiplexer_26_out, multiplexer_27_out, multiplexer_28_out, multiplexer_29_out, multiplexer_30_out,
       multiplexer_31_out, multiplexer_32_out;

  Multiplexer multiplexer_1 (.sel(En), .in_0(S[0]), .in_1(E[0]), .out(multiplexer_1_out));
  D_FF d_ff_1 (.D(multiplexer_1_out), .C(Clk), .Q(S[0]));  // open: nQ
  Multiplexer multiplexer_2 (.sel(En), .in_0(S[1]), .in_1(E[1]), .out(multiplexer_2_out));
  D_FF d_ff_2 (.D(multiplexer_2_out), .C(Clk), .Q(S[1]));  // open: nQ
  Multiplexer multiplexer_3 (.sel(En), .in_0(S[2]), .in_1(E[2]), .out(multiplexer_3_out));
  D_FF d_ff_3 (.D(multiplexer_3_out), .C(Clk), .Q(S[2]));  // open: nQ
  Multiplexer multiplexer_4 (.sel(En), .in_0(S[3]), .in_1(E[3]), .out(multiplexer_4_out));
  D_FF d_ff_4 (.D(multiplexer_4_out), .C(Clk), .Q(S[3]));  // open: nQ
  Multiplexer multiplexer_5 (.sel(En), .in_0(S[4]), .in_1(E[4]), .out(multiplexer_5_out));
  D_FF d_ff_5 (.D(multiplexer_5_out), .C(Clk), .Q(S[4]));  // open: nQ
  Multiplexer multiplexer_6 (.sel(En), .in_0(S[5]), .in_1(E[5]), .out(multiplexer_6_out));
  D_FF d_ff_6 (.D(multiplexer_6_out), .C(Clk), .Q(S[5]));  // open: nQ
  Multiplexer multiplexer_7 (.sel(En), .in_0(S[6]), .in_1(E[6]), .out(multiplexer_7_out));
  D_FF d_ff_7 (.D(multiplexer_7_out), .C(Clk), .Q(S[6]));  // open: nQ
  Multiplexer multiplexer_8 (.sel(En), .in_0(S[7]), .in_1(E[7]), .out(multiplexer_8_out));
  D_FF d_ff_8 (.D(multiplexer_8_out), .C(Clk), .Q(S[7]));  // open: nQ
  Multiplexer multiplexer_9 (.sel(En), .in_0(S[8]), .in_1(E[8]), .out(multiplexer_9_out));
  D_FF d_ff_9 (.D(multiplexer_9_out), .C(Clk), .Q(S[8]));  // open: nQ
  Multiplexer multiplexer_10 (.sel(En), .in_0(S[9]), .in_1(E[9]), .out(multiplexer_10_out));
  D_FF d_ff_10 (.D(multiplexer_10_out), .C(Clk), .Q(S[9]));  // open: nQ
  Multiplexer multiplexer_11 (.sel(En), .in_0(S[10]), .in_1(E[10]), .out(multiplexer_11_out));
  D_FF d_ff_11 (.D(multiplexer_11_out), .C(Clk), .Q(S[10]));  // open: nQ
  Multiplexer multiplexer_12 (.sel(En), .in_0(S[11]), .in_1(E[11]), .out(multiplexer_12_out));
  D_FF d_ff_12 (.D(multiplexer_12_out), .C(Clk), .Q(S[11]));  // open: nQ
  Multiplexer multiplexer_13 (.sel(En), .in_0(S[12]), .in_1(E[12]), .out(multiplexer_13_out));
  D_FF d_ff_13 (.D(multiplexer_13_out), .C(Clk), .Q(S[12]));  // open: nQ
  Multiplexer multiplexer_14 (.sel(En), .in_0(S[13]), .in_1(E[13]), .out(multiplexer_14_out));
  D_FF d_ff_14 (.D(multiplexer_14_out), .C(Clk), .Q(S[13]));  // open: nQ
  Multiplexer multiplexer_15 (.sel(En), .in_0(S[14]), .in_1(E[14]), .out(multiplexer_15_out));
  D_FF d_ff_15 (.D(multiplexer_15_out), .C(Clk), .Q(S[14]));  // open: nQ
  Multiplexer multiplexer_16 (.sel(En), .in_0(S[15]), .in_1(E[15]), .out(multiplexer_16_out));
  D_FF d_ff_16 (.D(multiplexer_16_out), .C(Clk), .Q(S[15]));  // open: nQ
  Multiplexer multiplexer_17 (.sel(En), .in_0(S[16]), .in_1(E[16]), .out(multiplexer_17_out));
  D_FF d_ff_17 (.D(multiplexer_17_out), .C(Clk), .Q(S[16]));  // open: nQ
  Multiplexer multiplexer_18 (.sel(En), .in_0(S[17]), .in_1(E[17]), .out(multiplexer_18_out));
  D_FF d_ff_18 (.D(multiplexer_18_out), .C(Clk), .Q(S[17]));  // open: nQ
  Multiplexer multiplexer_19 (.sel(En), .in_0(S[18]), .in_1(E[18]), .out(multiplexer_19_out));
  D_FF d_ff_19 (.D(multiplexer_19_out), .C(Clk), .Q(S[18]));  // open: nQ
  Multiplexer multiplexer_20 (.sel(En), .in_0(S[19]), .in_1(E[19]), .out(multiplexer_20_out));
  D_FF d_ff_20 (.D(multiplexer_20_out), .C(Clk), .Q(S[19]));  // open: nQ
  Multiplexer multiplexer_21 (.sel(En), .in_0(S[20]), .in_1(E[20]), .out(multiplexer_21_out));
  D_FF d_ff_21 (.D(multiplexer_21_out), .C(Clk), .Q(S[20]));  // open: nQ
  Multiplexer multiplexer_22 (.sel(En), .in_0(S[21]), .in_1(E[21]), .out(multiplexer_22_out));
  D_FF d_ff_22 (.D(multiplexer_22_out), .C(Clk), .Q(S[21]));  // open: nQ
  Multiplexer multiplexer_23 (.sel(En), .in_0(S[22]), .in_1(E[22]), .out(multiplexer_23_out));
  D_FF d_ff_23 (.D(multiplexer_23_out), .C(Clk), .Q(S[22]));  // open: nQ
  Multiplexer multiplexer_24 (.sel(En), .in_0(S[23]), .in_1(E[23]), .out(multiplexer_24_out));
  D_FF d_ff_24 (.D(multiplexer_24_out), .C(Clk), .Q(S[23]));  // open: nQ
  Multiplexer multiplexer_25 (.sel(En), .in_0(S[24]), .in_1(E[24]), .out(multiplexer_25_out));
  D_FF d_ff_25 (.D(multiplexer_25_out), .C(Clk), .Q(S[24]));  // open: nQ
  Multiplexer multiplexer_26 (.sel(En), .in_0(S[25]), .in_1(E[25]), .out(multiplexer_26_out));
  D_FF d_ff_26 (.D(multiplexer_26_out), .C(Clk), .Q(S[25]));  // open: nQ
  Multiplexer multiplexer_27 (.sel(En), .in_0(S[26]), .in_1(E[26]), .out(multiplexer_27_out));
  D_FF d_ff_27 (.D(multiplexer_27_out), .C(Clk), .Q(S[26]));  // open: nQ
  Multiplexer multiplexer_28 (.sel(En), .in_0(S[27]), .in_1(E[27]), .out(multiplexer_28_out));
  D_FF d_ff_28 (.D(multiplexer_28_out), .C(Clk), .Q(S[27]));  // open: nQ
  Multiplexer multiplexer_29 (.sel(En), .in_0(S[28]), .in_1(E[28]), .out(multiplexer_29_out));
  D_FF d_ff_29 (.D(multiplexer_29_out), .C(Clk), .Q(S[28]));  // open: nQ
  Multiplexer multiplexer_30 (.sel(En), .in_0(S[29]), .in_1(E[29]), .out(multiplexer_30_out));
  D_FF d_ff_30 (.D(multiplexer_30_out), .C(Clk), .Q(S[29]));  // open: nQ
  Multiplexer multiplexer_31 (.sel(En), .in_0(S[30]), .in_1(E[30]), .out(multiplexer_31_out));
  D_FF d_ff_31 (.D(multiplexer_31_out), .C(Clk), .Q(S[30]));  // open: nQ
  Multiplexer multiplexer_32 (.sel(En), .in_0(S[31]), .in_1(E[31]), .out(multiplexer_32_out));
  D_FF d_ff_32 (.D(multiplexer_32_out), .C(Clk), .Q(S[31]));  // open: nQ
endmodule
