// Digital circuit Shifter 2bits.dig as structural Verilog
module Shifter_2bits (
  input  [31:0] E,
  output [31:0] S
);

  wire [31:0] shifter_1bit_1_s;

  Shifter_1bit shifter_1bit_1 (.Sel(1'b1), .A(E), .S(shifter_1bit_1_s));
  Shifter_1bit shifter_1bit_2 (.Sel(1'b1), .A(shifter_1bit_1_s), .S(S));
endmodule
