// Digital circuit Shifter A >> B 32bits.dig as structural Verilog
module Shifter_A____B_32bits (
  input  [31:0] A,
  input  [31:0] B,
  output [31:0] S
);

  wire [5:5] or_1_out;
  wire [31:0] shift31, shifter_1bit_1_s, shifter_1bit_2_s, shifter_1bit_3_s, shifter_1bit_4_s,
       shifter_1bit_5_s, shifter_1bit_6_s, shifter_1bit_7_s, shifter_1bit_8_s, shifter_1bit_9_s,
       shifter_1bit_10_s, shifter_1bit_11_s, shifter_1bit_12_s, shifter_1bit_13_s, shifter_1bit_14_s,
       shifter_1bit_15_s, shifter_1bit_16_s, shifter_1bit_17_s, shifter_1bit_18_s, shifter_1bit_19_s,
       shifter_1bit_20_s, shifter_1bit_21_s, shifter_1bit_22_s, shifter_1bit_23_s, shifter_1bit_24_s,
       shifter_1bit_25_s, shifter_1bit_26_s, shifter_1bit_27_s, shifter_1bit_28_s, shifter_1bit_29_s,
       shifter_1bit_30_s, shifter_1bit_31_s;

  Shifter_1bit shifter_1bit_1 (.Sel(1'b1), .A(A), .S(shifter_1bit_1_s));
  Shifter_1bit shifter_1bit_2 (.Sel(1'b1), .A(shifter_1bit_1_s), .S(shifter_1bit_2_s));
  Shifter_1bit shifter_1bit_3 (.Sel(1'b1), .A(shifter_1bit_2_s), .S(shifter_1bit_3_s));
  Shifter_1bit shifter_1bit_4 (.Sel(1'b1), .A(shifter_1bit_3_s), .S(shifter_1bit_4_s));
  Shifter_1bit shifter_1bit_5 (.Sel(1'b1), .A(shifter_1bit_4_s), .S(shifter_1bit_5_s));
  Shifter_1bit shifter_1bit_6 (.Sel(1'b1), .A(shifter_1bit_5_s), .S(shifter_1bit_6_s));
  Shifter_1bit shifter_1bit_7 (.Sel(1'b1), .A(shifter_1bit_6_s), .S(shifter_1bit_7_s));
  Shifter_1bit shifter_1bit_8 (.Sel(1'b1), .A(shifter_1bit_7_s), .S(shifter_1bit_8_s));
  Shifter_1bit shifter_1bit_9 (.Sel(1'b1), .A(shifter_1bit_8_s), .S(shifter_1bit_9_s));
  Shifter_1bit shifter_1bit_10 (.Sel(1'b1), .A(shifter_1bit_9_s), .S(shifter_1bit_10_s));
  Shifter_1bit shifter_1bit_11 (.Sel(1'b1), .A(shifter_1bit_10_s), .S(shifter_1bit_11_s));
  Shifter_1bit shifter_1bit_12 (.Sel(1'b1), .A(shifter_1bit_11_s), .S(shifter_1bit_12_s));
  Shifter_1bit shifter_1bit_13 (.Sel(1'b1), .A(shifter_1bit_12_s), .S(shifter_1bit_13_s));
  Shifter_1bit shifter_1bit_14 (.Sel(1'b1), .A(shifter_1bit_13_s), .S(shifter_1bit_14_s));
  Shifter_1bit shifter_1bit_15 (.Sel(1'b1), .A(shifter_1bit_14_s), .S(shifter_1bit_15_s));
  Shifter_1bit shifter_1bit_16 (.Sel(1'b1), .A(shifter_1bit_15_s), .S(shifter_1bit_16_s));
  Shifter_1bit shifter_1bit_17 (.Sel(1'b1), .A(shifter_1bit_16_s), .S(shifter_1bit_17_s));
  Shifter_1bit shifter_1bit_18 (.Sel(1'b1), .A(shifter_1bit_17_s), .S(shifter_1bit_18_s));
  Shifter_1bit shifter_1bit_19 (.Sel(1'b1), .A(shifter_1bit_18_s), .S(shifter_1bit_19_s));
  Shifter_1bit shifter_1bit_20 (.Sel(1'b1), .A(shifter_1bit_19_s), .S(shifter_1bit_20_s));
  Shifter_1bit shifter_1bit_21 (.Sel(1'b1), .A(shifter_1bit_20_s), .S(shifter_1bit_21_s));
  Shifter_1bit shifter_1bit_22 (.Sel(1'b1), .A(shifter_1bit_21_s), .S(shifter_1bit_22_s));
  Shifter_1bit shifter_1bit_23 (.Sel(1'b1), .A(shifter_1bit_22_s), .S(shifter_1bit_23_s));
  Shifter_1bit shifter_1bit_24 (.Sel(1'b1), .A(shifter_1bit_23_s), .S(shifter_1bit_24_s));
  Shifter_1bit shifter_1bit_25 (.Sel(1'b1), .A(shifter_1bit_24_s), .S(shifter_1bit_25_s));
  Shifter_1bit shifter_1bit_26 (.Sel(1'b1), .A(shifter_1bit_25_s), .S(shifter_1bit_26_s));
  Shifter_1bit shifter_1bit_27 (.Sel(1'b1), .A(shifter_1bit_26_s), .S(shifter_1bit_27_s));
  Shifter_1bit shifter_1bit_28 (.Sel(1'b1), .A(shifter_1bit_27_s), .S(shifter_1bit_28_s));
  Shifter_1bit shifter_1bit_29 (.Sel(1'b1), .A(shifter_1bit_28_s), .S(shifter_1bit_29_s));
  Shifter_1bit shifter_1bit_30 (.Sel(1'b1), .A(shifter_1bit_29_s), .S(shifter_1bit_30_s));
  Shifter_1bit shifter_1bit_31 (.Sel(1'b1), .A(shifter_1bit_30_s), .S(shifter_1bit_31_s));
  Shifter_1bit shifter_1bit_32 (.Sel(1'b1), .A(shifter_1bit_31_s), .S(shift31));
  Multiplexer #(.Selector_Bits(6), .Bits(32)) multiplexer_1 (
    .sel({or_1_out[5], B[4:0]}), .in_0(A), .in_1(shifter_1bit_1_s), .in_2(shifter_1bit_2_s),
    .in_3(shifter_1bit_3_s), .in_4(shifter_1bit_4_s), .in_5(shifter_1bit_5_s), .in_6(shifter_1bit_6_s),
    .in_7(shifter_1bit_7_s), .in_8(shifter_1bit_8_s), .in_9(shifter_1bit_9_s), .in_10(shifter_1bit_10_s),
    .in_11(shifter_1bit_11_s), .in_12(shifter_1bit_12_s), .in_13(shifter_1bit_13_s),
    .in_14(shifter_1bit_14_s), .in_15(shifter_1bit_15_s), .in_16(shifter_1bit_16_s),
    .in_17(shifter_1bit_17_s), .in_18(shifter_1bit_18_s), .in_19(shifter_1bit_19_s),
    .in_20(shifter_1bit_20_s), .in_21(shifter_1bit_21_s), .in_22(shifter_1bit_22_s),
    .in_23(shifter_1bit_23_s), .in_24(shifter_1bit_24_s), .in_25(shifter_1bit_25_s),
    .in_26(shifter_1bit_26_s), .in_27(shifter_1bit_27_s), .in_28(shifter_1bit_28_s),
    .in_29(shifter_1bit_29_s), .in_30(shifter_1bit_30_s), .in_31(shifter_1bit_31_s), .in_32(shift31),
    .in_33(shift31), .in_34(shift31), .in_35(shift31), .in_36(shift31), .in_37(shift31), .in_38(shift31),
    .in_39(shift31), .in_40(shift31), .in_41(shift31), .in_42(shift31), .in_43(shift31), .in_44(shift31),
    .in_45(shift31), .in_46(shift31), .in_47(shift31), .in_48(shift31), .in_49(shift31), .in_50(shift31),
    .in_51(shift31), .in_52(shift31), .in_53(shift31), .in_54(shift31), .in_55(shift31), .in_56(shift31),
    .in_57(shift31), .in_58(shift31), .in_59(shift31), .in_60(shift31), .in_61(shift31), .in_62(shift31),
    .in_63(shift31), .out(S));
  or or_1 (or_1_out[5], B[31], B[30], B[29], B[28], B[27], B[26], B[25], B[24], B[23], B[22], B[21], B[20], B[19], B[18], B[17], B[16], B[15], B[14], B[13], B[12], B[11], B[10], B[9], B[8], B[7], B[6], B[5]);
endmodule
