// Digital circuit ULA 32bits.dig as structural Verilog
module ULA_32bits (
  input  [31:0] A,
  input  [31:0] B,
  input  [3:0] funct,
  output [31:0] S,
  output Zero
);

  wire [31:0] and_32bits_1_s, full_adder_32bits_1_s, full_subtractor_32bits_1_s, mul_32bits_1_s,
       or_32bits_1_s, shifter_a____b_32bits_1_s, xor_32bits_1_s;

  Full_Adder_32bits full_adder_32bits_1 (.A(A), .B(B), .S(full_adder_32bits_1_s));  // open: cout
  Full_Subtractor_32bits full_subtractor_32bits_1 (.A(A), .B(B), .S(full_subtractor_32bits_1_s));  // open: bout
  Mul_32bits mul_32bits_1 (.A(A), .B(B), .S(mul_32bits_1_s));
  AND_32bits and_32bits_1 (.A(A), .B(B), .S(and_32bits_1_s));
  OR_32bits or_32bits_1 (.A(A), .B(B), .S(or_32bits_1_s));
  XOR_32bits xor_32bits_1 (.A(A), .B(B), .S(xor_32bits_1_s));
  Shifter_A____B_32bits shifter_a____b_32bits_1 (.A(A), .B(B), .S(shifter_a____b_32bits_1_s));
  Multiplexer #(.Selector_Bits(4), .Bits(32)) multiplexer_1 (
    .sel(funct), .in_0(full_adder_32bits_1_s), .in_1(full_subtractor_32bits_1_s), .in_2(mul_32bits_1_s),
    .in_3(and_32bits_1_s), .in_4(or_32bits_1_s), .in_5(xor_32bits_1_s), .in_6(shifter_a____b_32bits_1_s),
    .in_7(B), .in_8({32{1'b0}}), .in_9(A), .in_10(A), .in_11(A), .in_12(A), .in_13(A), .in_14(A), .in_15(A),
    .out(S));
  or or_1 (Zero, S[0], S[1], S[2], S[3], S[4], S[5], S[6], S[7], S[8], S[9], S[10], S[11], S[12], S[13], S[14], S[15], S[17], S[18], S[19], S[20], S[21], S[22], S[23], S[24], S[25], S[26], S[27], S[28], S[29], S[30], S[31], S[16]);

  // Notes on the sheet:
  //   Caso todos sejam 0, passa sinal lógico 0
endmodule
