// Digital circuit XOR 32bits.dig as structural Verilog
module XOR_32bits (
  input  [31:0] A,
  input  [31:0] B,
  output [31:0] S
);

  XOR_1bit xor_1bit_1 (.A(A[0]), .B(B[0]), .S(S[0]));
  XOR_1bit xor_1bit_2 (.A(A[1]), .B(B[1]), .S(S[1]));
  XOR_1bit xor_1bit_3 (.A(A[2]), .B(B[2]), .S(S[2]));
  XOR_1bit xor_1bit_4 (.A(A[3]), .B(B[3]), .S(S[3]));
  XOR_1bit xor_1bit_5 (.A(A[4]), .B(B[4]), .S(S[4]));
  XOR_1bit xor_1bit_6 (.A(A[5]), .B(B[5]), .S(S[5]));
  XOR_1bit xor_1bit_7 (.A(A[6]), .B(B[6]), .S(S[6]));
  XOR_1bit xor_1bit_8 (.A(A[7]), .B(B[7]), .S(S[7]));
  XOR_1bit xor_1bit_9 (.A(A[8]), .B(B[8]), .S(S[8]));
  XOR_1bit xor_1bit_10 (.A(A[9]), .B(B[9]), .S(S[9]));
  XOR_1bit xor_1bit_11 (.A(A[10]), .B(B[10]), .S(S[10]));
  XOR_1bit xor_1bit_12 (.A(A[11]), .B(B[11]), .S(S[11]));
  XOR_1bit xor_1bit_13 (.A(A[12]), .B(B[12]), .S(S[12]));
  XOR_1bit xor_1bit_14 (.A(A[13]), .B(B[13]), .S(S[13]));
  XOR_1bit xor_1bit_15 (.A(A[14]), .B(B[14]), .S(S[14]));
  XOR_1bit xor_1bit_16 (.A(A[15]), .B(B[15]), .S(S[15]));
  XOR_1bit xor_1bit_17 (.A(A[16]), .B(B[16]), .S(S[16]));
  XOR_1bit xor_1bit_18 (.A(A[17]), .B(B[17]), .S(S[17]));
  XOR_1bit xor_1bit_19 (.A(A[18]), .B(B[18]), .S(S[18]));
  XOR_1bit xor_1bit_20 (.A(A[19]), .B(B[19]), .S(S[19]));
  XOR_1bit xor_1bit_21 (.A(A[20]), .B(B[20]), .S(S[20]));
  XOR_1bit xor_1bit_22 (.A(A[21]), .B(B[21]), .S(S[21]));
  XOR_1bit xor_1bit_23 (.A(A[22]), .B(B[22]), .S(S[22]));
  XOR_1bit xor_1bit_24 (.A(A[23]), .B(B[23]), .S(S[23]));
  XOR_1bit xor_1bit_25 (.A(A[24]), .B(B[24]), .S(S[24]));
  XOR_1bit xor_1bit_26 (.A(A[25]), .B(B[25]), .S(S[25]));
  XOR_1bit xor_1bit_27 (.A(A[26]), .B(B[26]), .S(S[26]));
  XOR_1bit xor_1bit_28 (.A(A[27]), .B(B[27]), .S(S[27]));
  XOR_1bit xor_1bit_29 (.A(A[28]), .B(B[28]), .S(S[28]));
  XOR_1bit xor_1bit_30 (.A(A[29]), .B(B[29]), .S(S[29]));
  XOR_1bit xor_1bit_31 (.A(A[30]), .B(B[30]), .S(S[30]));
  XOR_1bit xor_1bit_32 (.A(A[31]), .B(B[31]), .S(S[31]));
endmodule
